// Logisim project control-logic.circ as structural Verilog: 1 circuit, main circuit control_logic
module control_logic (
  input  [31:0] Instruction,
  input  BrEq,
  input  BrLt,
  output PCSel,
  output RegWEn,
  output [2:0] ImmSel,
  output BrUn,
  output ASel,
  output BSel,
  output [3:0] ALUSel,
  output MemWEn,
  output [1:0] WBSel
);

  wire comparator_1_eq, comparator_2_eq, comparator_3_eq, demultiplexer_1_out1, demultiplexer_1_out5,
       is_addi, is_andi, is_ori, is_slli, is_slti, is_srai, is_srli, is_xori;
  wire [5:0] RomInput;
  wire [15:14] rom_1_data;

  ROM #(.addrWidth(6), .dataWidth(16)) rom_1 (
    .addr(RomInput), .data({rom_1_data, WBSel, MemWEn, ALUSel, BSel, ASel, BrUn, ImmSel, RegWEn}));
  Comparator #(.width(7)) comparator_1 (.a({7{1'b0}}), .b(Instruction[31:25]), .eq(comparator_1_eq));  // open: gt, lt
  Demultiplexer #(.select(3)) demultiplexer_1 (
    .out0(is_addi), .out1(demultiplexer_1_out1), .out2(is_slti), .out4(is_xori), .out5(demultiplexer_1_out5),
    .out6(is_ori), .out7(is_andi), .in(1'b1), .sel(Instruction[14:12]));  // open: out3
  and and_1 (is_slli, demultiplexer_1_out1, comparator_1_eq);
  Comparator #(.width(7)) comparator_2 (.a({7{1'b0}}), .b(Instruction[31:25]), .eq(comparator_2_eq));  // open: gt, lt
  and and_2 (is_srli, demultiplexer_1_out5, comparator_2_eq);
  Comparator #(.width(7)) comparator_3 (.a(7'b0100000), .b(Instruction[31:25]), .eq(comparator_3_eq));  // open: gt, lt
  and and_3 (is_srai, demultiplexer_1_out5, comparator_3_eq);
  Priority_Encoder #(.select_enc(6)) priority_encoder_1 (
    .in15(is_addi), .in16(is_slli), .in17(is_slti), .in18(is_xori), .in19(is_srli), .in20(is_srai),
    .in21(is_ori), .in22(is_andi), .out(RomInput));  // open: in0, in1, in2, in3, in4, in5, in6, in7, in8, in9, in10, in11, in12, in13, in14, in23, in24, in25, in26, in27, in28, in29, in30, in31, in32, in33, in34, in35, in36, in37, in38, in39, in40, in41, in42, in43, in44, in45, in46, in47, in48, in49, in50, in51, in52, in53, in54, in55, in56, in57, in58, in59, in60, in61, in62, in63, gs, en_out, en_in

  assign PCSel = 1'b0;

  // Notes on the sheet:
  //   INPUTS to your circuit
  //   contents of rom_1 (hex, n*v repeats v):
  //   15*0 1041 10c1 1141 1241 12c1 16c1 1341 13c1
  //   ROM FOR CONTROL LOGIC
  //   DON'T CHANGE THE LOCATIONS OF THE INPUTS AND OUTPUTS!
  //   This is only if you choose to do the ROM option
  //   OUTPUT from your circuit
  //   Reminder: If using ROM, use combinational logic for PCSel
endmodule
